// Logisim project rotate_right.circ as structural Verilog: 6 circuits, main circuit main
module main (
  input  [15:0] in_1,
  input  [3:0] in_2,
  output [15:0] out_3
);

  ROTR rotr_1 (.DATA(in_1), .SHIFT(in_2), .OUTPUT_0(out_3));
endmodule

module ROTR (
  input  [15:0] DATA,
  input  [3:0] SHIFT,
  output [15:0] OUTPUT_0
);

  wire [15:0] rotr_2_1_output_0, rotr_4_1_output_0, rotr_8_1_output_0;

  ROTR_8 rotr_8_1 (.DATA(DATA), .SHIFT(SHIFT[3]), .OUTPUT_0(rotr_8_1_output_0));
  ROTR_4 rotr_4_1 (.DATA(rotr_8_1_output_0), .SHIFT(SHIFT[2]), .OUTPUT_0(rotr_4_1_output_0));
  ROTR_2 rotr_2_1 (.DATA(rotr_4_1_output_0), .SHIFT(SHIFT[1]), .OUTPUT_0(rotr_2_1_output_0));
  ROTR_1 rotr_1_1 (.DATA(rotr_2_1_output_0), .SHIFT(SHIFT[0]), .OUTPUT_0(OUTPUT_0));
endmodule

module ROTR_8 (
  input  [15:0] DATA,
  input  SHIFT,
  output [15:0] OUTPUT_0
);

  Multiplexer #(.width(16), .enable("false")) multiplexer_1 (
    .in0(DATA), .in1({DATA[7:0], DATA[15:8]}), .out(OUTPUT_0), .sel(SHIFT));
endmodule

module ROTR_4 (
  input  [15:0] DATA,
  input  SHIFT,
  output [15:0] OUTPUT_0
);

  Multiplexer #(.width(16), .enable("false")) multiplexer_1 (
    .in0(DATA), .in1({DATA[3:0], DATA[15:4]}), .out(OUTPUT_0), .sel(SHIFT));
endmodule

module ROTR_2 (
  input  [15:0] DATA,
  input  SHIFT,
  output [15:0] OUTPUT_0
);

  Multiplexer #(.width(16), .enable("false")) multiplexer_1 (
    .in0(DATA), .in1({DATA[1:0], DATA[15:2]}), .out(OUTPUT_0), .sel(SHIFT));
endmodule

module ROTR_1 (
  input  [15:0] DATA,
  input  SHIFT,
  output [15:0] OUTPUT_0
);

  Multiplexer #(.width(16), .enable("false")) multiplexer_1 (
    .in0(DATA), .in1({DATA[0], DATA[15:1]}), .out(OUTPUT_0), .sel(SHIFT));
endmodule
