// Logisim project splitters.circ as structural Verilog
module Ex4 (
  input  [7:0] In1,
  output Out1,
  output [7:0] Out2
);

  and and_1 (Out1, In1[0], In1[7]);
  not not_1 (Out2[7], In1[7]);

  assign Out2[6:0] = In1[6:0];
endmodule
