// Logisim project store_element.circ as structural Verilog: 2 circuits, main circuit main
module main (
  output [7:0] out_1,
  output [7:0] out_2
);

  AddMachine addmachine_1 (.MEMORY_OUTPUT(out_1), .ADDER_OUTPUT(out_2));
endmodule

module AddMachine (
  output [7:0] MEMORY_OUTPUT,
  output [7:0] ADDER_OUTPUT
);

  wire clock_1_out;

  Adder adder_1 (.a(MEMORY_OUTPUT), .b(8'h1), .out(ADDER_OUTPUT));  // open: cin, cout
  Clock clock_1 (.out(clock_1_out));
  Register register_1 (.D(ADDER_OUTPUT), .clk(clock_1_out), .Q(MEMORY_OUTPUT));  // open: en, clr
endmodule
