// Logisim project sub_circuits.circ as structural Verilog: 6 circuits, main circuit main
module main (
  input  in_1,
  input  in_2,
  input  in_3,
  input  in_4,
  input  in_5,
  input  in_6,
  input  in_7,
  input  in_8,
  input  in_9,
  output out_10,
  output out_11,
  output out_12,
  output out_13,
  output out_14
);

  NAND1 nand1_1 (.Input0(in_1), .Input1(in_2), .Ouput0(out_10));
  NOR1 nor1_1 (.Input0(in_1), .Input1(in_2), .Output0(out_11));
  XOR1 xor1_1 (.Input0(in_1), .Input1(in_2), .Output0(out_12));
  MUX_2_1 mux_2_1_1 (.INPUT0(in_1), .INPUT1(in_2), .SELECT0(in_3), .OUTPUT0(out_13));
  MUX_4_1 mux_4_1_1 (
    .Input0(in_4), .Input1(in_5), .INPUT2(in_6), .INPUT3(in_7), .SELECT0(in_8), .SELECT1(in_9),
    .Output0(out_14));
endmodule

module NAND1 (
  input  Input0,
  input  Input1,
  output Ouput0
);

  wire and_1_out;

  and and_1 (and_1_out, Input0, Input1);
  not not_1 (Ouput0, and_1_out);
endmodule

module NOR1 (
  input  Input0,
  input  Input1,
  output Output0
);

  wire or_1_out;

  or or_1 (or_1_out, Input0, Input1);
  not not_1 (Output0, or_1_out);
endmodule

module XOR1 (
  input  Input0,
  input  Input1,
  output Output0
);

  wire and_1_out, and_2_out, not_1_out, not_2_out;

  not not_1 (not_1_out, Input1);
  not not_2 (not_2_out, Input0);
  and and_1 (and_1_out, Input0, not_1_out);
  and and_2 (and_2_out, Input1, not_2_out);
  or or_1 (Output0, and_1_out, and_2_out);
endmodule

module MUX_2_1 (
  input  INPUT0,
  input  INPUT1,
  input  SELECT0,
  output OUTPUT0
);

  wire and_1_out, and_2_out, not_1_out;

  not not_1 (not_1_out, SELECT0);
  and and_1 (and_1_out, INPUT0, not_1_out);
  and and_2 (and_2_out, INPUT1, SELECT0);
  or or_1 (OUTPUT0, and_1_out, and_2_out);
endmodule

module MUX_4_1 (
  input  Input0,
  input  Input1,
  input  INPUT2,
  input  INPUT3,
  input  SELECT0,
  input  SELECT1,
  output Output0
);

  wire and_1_out, and_2_out, and_3_out, and_4_out, not_1_out, not_2_out, not_3_out, not_4_out;

  not not_1 (not_1_out, SELECT0);
  not not_2 (not_2_out, SELECT1);
  not not_3 (not_3_out, SELECT1);
  not not_4 (not_4_out, SELECT0);
  and and_1 (and_1_out, Input0, not_1_out, not_2_out);
  and and_2 (and_2_out, Input1, SELECT0, not_3_out);
  and and_3 (and_3_out, INPUT2, not_4_out, SELECT1);
  and and_4 (and_4_out, INPUT3, SELECT0, SELECT1);
  or or_1 (Output0, and_1_out, and_2_out, and_3_out, and_4_out);
endmodule
