// Logisim project alu.circ as structural Verilog: 1 circuit, main circuit alu
module alu (
  input  [31:0] A,
  input  [31:0] B,
  input  [3:0] ALUSel,
  output [31:0] Result
);

  wire [0:0] SLT_32;
  wire [31:0] ADD_32, adder_2_out, AND_32, DIVU_32, MULH_32, MULHU_32, MULT_32, multiplexer_1_out,
       multiplexer_2_out, negator_1_out, negator_2_out, OR_32, REMU_32, SLL_32, SRA_32, SRL_32, SUB_32,
       XOR_32;

  Adder #(.width(32)) adder_1 (.a(A), .b(B), .out(ADD_32));  // open: cin, cout
  assign AND_32 = A & B;  // AND_Gate and_1, 32 bits wide
  assign OR_32 = A | B;  // OR_Gate or_1, 32 bits wide
  assign XOR_32 = A ^ B;  // XOR_Gate xor_1, 32 bits wide
  Shifter #(.width(32), .shift("lr")) shifter_1 (.in(A), .\dist (B[4:0]), .out(SRL_32));
  Shifter #(.width(32), .shift("ar")) shifter_2 (.in(A), .\dist (B[4:0]), .out(SRA_32));
  Shifter #(.width(32)) shifter_3 (.in(A), .\dist (B[4:0]), .out(SLL_32));
  Comparator #(.width(32)) comparator_1 (.a(A), .b(B), .lt(SLT_32[0]));  // open: gt, eq
  Divider #(.width(32)) divider_1 (.a(A), .b(B), .out(DIVU_32), .rem(REMU_32));  // open: upper
  Multiplier #(.width(32)) multiplier_1 (.a(A), .b(B), .out(MULT_32), .cout(MULHU_32));  // open: cin
  Subtractor #(.width(32)) subtractor_1 (.a(A), .b(B), .out(SUB_32));  // open: bin, bout
  Negator #(.width(32)) negator_1 (.in(A), .out(negator_1_out));
  Negator #(.width(32)) negator_2 (.in(B), .out(negator_2_out));
  Multiplexer #(.width(32), .enable("false")) multiplexer_1 (
    .in0({32{1'b0}}), .in1(negator_2_out), .out(multiplexer_1_out), .sel(A[31]));
  Multiplexer #(.width(32), .enable("false")) multiplexer_2 (
    .in0({32{1'b0}}), .in1(negator_1_out), .out(multiplexer_2_out), .sel(B[31]));
  Adder #(.width(32)) adder_2 (.a(multiplexer_2_out), .b(multiplexer_1_out), .out(adder_2_out));  // open: cin, cout
  Adder #(.width(32)) adder_3 (.a(MULHU_32), .b(adder_2_out), .out(MULH_32));  // open: cin, cout
  Multiplexer #(.select(4), .width(32), .enable("false")) multiplexer_3 (
    .in0(ADD_32), .in1(AND_32), .in2(OR_32), .in3(XOR_32), .in4(SRL_32), .in5(SRA_32), .in6(SLL_32),
    .in7({{31{1'b0}}, SLT_32[0]}), .in8(DIVU_32), .in9(REMU_32), .in10(MULT_32), .in11(MULHU_32),
    .in12(SUB_32), .in13(B), .in14(MULH_32), .out(Result), .sel(ALUSel));  // open: in15

  // Notes on the sheet:
  //   INPUTS to your circuit
  //   DON'T CHANGE THE LOCATIONS OF THE INPUTS AND OUTPUTS!
  //   OUTPUT from your circuit
endmodule
